# Fritzing sketch BranchesDiagram (saved by Fritzing 0.9.9b)
breadboards: 1

parts:
  Part1 = Arduino Nano (Rev3.0) (ICSP)
  J1 = Basic Servo
  VCC1 = 4 x AAA Battery Mount

nets:
  GND: Part1.GND, J1.gnd, VCC1.-
  N1: Part1.D9, J1.pulse
  N2: J1.vcc, VCC1.+
